// Logisim project smips.circ as structural Verilog: 9 circuits, main circuit Board
module Board (
);

  wire CLK, HALT, MEM_WE, RESET, TTY_WE;
  wire [3:0] MEM_BE;
  wire [6:0] TTY_DATA;
  wire [31:0] MEM_ADDR, MEM_RDATA, MEM_WDATA;

  Clock Reloj (.out(CLK));
  Button u_Reset (.out(RESET));
  CPU cpu_1 (
    .CLK(CLK), .RESET(RESET), .MEM_RDATA(MEM_RDATA), .MEM_ADDR(MEM_ADDR), .MEM_WDATA(MEM_WDATA),
    .MEM_BE(MEM_BE), .MEM_WE(MEM_WE), .TTY_DATA(TTY_DATA), .TTY_WE(TTY_WE), .HALT(HALT));
  TTY #(.cols(48), .rows(12)) tty_1 (.data(TTY_DATA), .clk(CLK), .we(TTY_WE), .clr(RESET));
  Memory memory_1 (.CLK(CLK), .ADDR(MEM_ADDR), .WDATA(MEM_WDATA), .BE(MEM_BE), .WE(MEM_WE), .RDATA(MEM_RDATA));
  LED u_Halt (.in(HALT));

  // Notes on the sheet:
  //   S-MIPS | Board
  //   No modificar: la CPU se implementa dentro del subcircuito CPU.
endmodule

module CPU (
  input  CLK,
  input  RESET,
  input  [31:0] MEM_RDATA,
  output [31:0] MEM_ADDR,
  output [31:0] MEM_WDATA,
  output [3:0] MEM_BE,
  output MEM_WE,
  output [6:0] TTY_DATA,
  output TTY_WE,
  output HALT
);

  Control_Unit control_unit_1 ();  // open: IRWRITE, ADDRSEL, PCSRC, PCWRITE, BRANCH, ALUSRCA, ALUSRCB, ALUOP, REGWRITE, REGDST, WDSEL, SYSSEL, MEM_WE, TTY_WE, HALT
  Instruction_Decoder instruction_decoder_1 ();  // open: OP, FUNCT, CLASS, ALUOP, EXTZERO, BNE, BYTE, UNSIGNED
  Branch_Control branch_control_1 ();  // open: PC_EN
  Datapath datapath_1 ();  // open: MEM_ADDR, MEM_WDATA, MEM_BE, OP, FUNCT, ZERO, V0_IS_10, V0_IS_11, TTY_DATA

  // Notes on the sheet:
  //   CPU S-MIPS: implementar aqui
  //   No cambiar nombres, anchos ni sentido de los pines: la placa depende de ellos.
endmodule

module Memory (
  input  CLK,
  input  [31:0] ADDR,
  input  [31:0] WDATA,
  input  [3:0] BE,
  input  WE,
  output [31:0] RDATA
);

  RAM #(.addrWidth(12), .asyncread("true"), .byteenables("byteEnables"), .dataWidth(32), .\type ("nonvolatile")) Main_Memory (
    .addr(ADDR[13:2]), .we(WE), .oe(1'b1), .clk(CLK), .din(WDATA), .dout(RDATA), .be3(BE[3]), .be2(BE[2]),
    .be1(BE[1]), .be0(BE[0]));

  // Other names for the same wires on the sheet: A[11:0] = ADDR[13:2]

  // Notes on the sheet:
  //   Memoria unificada: 4096 palabras de 32 bits (16 KiB), little-endian
  //   Lectura combinacional; escritura en el flanco de subida de CLK con WE=1, solo en los bytes con BE=1.
  //   Se usan los bits 13..2 de ADDR; los demas se ignoran (el espacio se repite cada 16 KiB).
endmodule

module Instruction_Decoder (
  input  [5:0] OP,
  input  [5:0] FUNCT,
  output [3:0] CLASS,
  output [2:0] ALUOP,
  output EXTZERO,
  output BNE,
  output BYTE,
  output UNSIGNED
);
endmodule

module Control_Unit (
  output IRWRITE,
  output ADDRSEL,
  output [1:0] PCSRC,
  output PCWRITE,
  output BRANCH,
  output [1:0] ALUSRCA,
  output [2:0] ALUSRCB,
  output [2:0] ALUOP,
  output REGWRITE,
  output [1:0] REGDST,
  output [1:0] WDSEL,
  output SYSSEL,
  output MEM_WE,
  output TTY_WE,
  output HALT
);
endmodule

module Branch_Control (
  output PC_EN
);
endmodule

module Datapath (
  output [31:0] MEM_ADDR,
  output [31:0] MEM_WDATA,
  output [3:0] MEM_BE,
  output [5:0] OP,
  output [5:0] FUNCT,
  output ZERO,
  output V0_IS_10,
  output V0_IS_11,
  output [6:0] TTY_DATA
);

  Register_File register_file_1 ();  // open: RD1, RD2
  ALU alu_1 ();  // open: A, B, OP, RESULT, ZERO
endmodule

module Register_File (
  output [31:0] RD1,
  output [31:0] RD2
);
endmodule

module ALU (
  input  [31:0] A,
  input  [31:0] B,
  input  [2:0] OP,
  output [31:0] RESULT,
  output ZERO
);
endmodule
